// Logisim project adder.circ as structural Verilog: 3 circuits, main circuit Half_Adder
module Half_Adder (
  input  C_In,
  input  A,
  input  B,
  output S,
  output C_Out
);

  wire and_1_out, and_2_out, xor_1_out;

  xor xor_1 (xor_1_out, A, B);
  xor xor_2 (S, xor_1_out, C_In);
  and and_1 (and_1_out, C_In, xor_1_out);
  and and_2 (and_2_out, A, B);
  or or_1 (C_Out, and_1_out, and_2_out);
endmodule

module Full_Adder_8_bit (
  input  C_In,
  input  B0,
  input  A0,
  input  A1,
  input  B1,
  input  A2,
  input  B2,
  input  A3,
  input  B3,
  input  A4,
  input  B4,
  input  A5,
  input  B5,
  input  A6,
  input  B6,
  input  A7,
  input  B7,
  output S0,
  output S1,
  output S2,
  output S3,
  output S4,
  output S5,
  output S6,
  output S7,
  output C_Out
);

  wire half_adder_1_c_out, half_adder_2_c_out, half_adder_3_c_out, half_adder_4_c_out, half_adder_5_c_out,
       half_adder_6_c_out, half_adder_7_c_out;

  Half_Adder half_adder_1 (.C_In(C_In), .A(B0), .B(A0), .S(S0), .C_Out(half_adder_1_c_out));
  Half_Adder half_adder_2 (.C_In(half_adder_1_c_out), .A(A1), .B(B1), .S(S1), .C_Out(half_adder_2_c_out));
  Half_Adder half_adder_3 (.C_In(half_adder_2_c_out), .A(A2), .B(B2), .S(S2), .C_Out(half_adder_3_c_out));
  Half_Adder half_adder_4 (.C_In(half_adder_3_c_out), .A(A3), .B(B3), .S(S3), .C_Out(half_adder_4_c_out));
  Half_Adder half_adder_5 (.C_In(half_adder_4_c_out), .A(A4), .B(B4), .S(S4), .C_Out(half_adder_5_c_out));
  Half_Adder half_adder_6 (.C_In(half_adder_5_c_out), .A(A5), .B(B5), .S(S5), .C_Out(half_adder_6_c_out));
  Half_Adder half_adder_7 (.C_In(half_adder_6_c_out), .A(A6), .B(B6), .S(S6), .C_Out(half_adder_7_c_out));
  Half_Adder half_adder_8 (.C_In(half_adder_7_c_out), .A(A7), .B(B7), .S(S7), .C_Out(C_Out));
endmodule

module Full_Adder_16_bit (
  input  C_In,
  input  A0,
  input  B0,
  input  A1,
  input  B1,
  input  A2,
  input  B2,
  input  A3,
  input  B3,
  input  A4,
  input  B4,
  input  A5,
  input  B5,
  input  A6,
  input  B6,
  input  A7,
  input  B7,
  input  A8,
  input  B8,
  input  A9,
  input  B9,
  input  A10,
  input  B10,
  input  A11,
  input  B11,
  input  A12,
  input  B12,
  input  A13,
  input  B13,
  input  A14,
  input  B14,
  input  A15,
  input  B15,
  output S0,
  output S1,
  output S2,
  output S3,
  output S4,
  output S5,
  output S6,
  output S7,
  output S8,
  output S9,
  output S10,
  output S11,
  output S12,
  output S13,
  output S14,
  output S15,
  output C_Out
);

  wire full_adder_8_bit_1_c_out;

  Full_Adder_8_bit full_adder_8_bit_1 (
    .C_In(C_In), .B0(A0), .A0(B0), .A1(A1), .B1(B1), .A2(A2), .B2(B2), .A3(A3), .B3(B3), .A4(A4), .B4(B4),
    .A5(A5), .B5(B5), .A6(A6), .B6(B6), .A7(A7), .B7(B7), .S0(S0), .S1(S1), .S2(S2), .S3(S3), .S4(S4),
    .S5(S5), .S6(S6), .S7(S7), .C_Out(full_adder_8_bit_1_c_out));
  Full_Adder_8_bit full_adder_8_bit_2 (
    .C_In(full_adder_8_bit_1_c_out), .B0(A8), .A0(B8), .A1(A9), .B1(B9), .A2(A10), .B2(B10), .A3(A11),
    .B3(B11), .A4(A12), .B4(B12), .A5(A13), .B5(B13), .A6(A14), .B6(B14), .A7(A15), .B7(B15), .S0(S8),
    .S1(S9), .S2(S10), .S3(S11), .S4(S12), .S5(S13), .S6(S14), .S7(S15), .C_Out(C_Out));
endmodule
