// Logisim project half_adder.circ as structural Verilog: 1 circuit, main circuit Half_Adder
module Half_Adder (
  input  A,
  input  B,
  input  C_In,
  output S,
  output C_Out
);

  wire and_1_out, and_2_out, xor_1_out;

  xor xor_1 (xor_1_out, A, B);
  xor xor_2 (S, xor_1_out, C_In);
  and and_1 (and_1_out, C_In, xor_1_out);
  and and_2 (and_2_out, A, B);
  or or_1 (C_Out, and_1_out, and_2_out);
endmodule
