// Logisim project nand.circ as structural Verilog: 5 circuits, main circuit nand_xor
module nand_xor (
  input  in_1,
  input  in_2,
  output out_3
);

  wire nand_1_out, nand_2_out, nand_3_out;

  nand nand_1 (nand_1_out, in_1, in_2);
  nand nand_2 (nand_2_out, in_1, nand_1_out);
  nand nand_3 (nand_3_out, nand_1_out, in_2);
  nand nand_4 (out_3, nand_2_out, nand_3_out);
endmodule

module flip_flop (
  input  in_1,
  input  in_2,
  output Q
);

  wire nand_2_out;

  nand nand_1 (Q, in_1, nand_2_out);
  nand nand_2 (nand_2_out, Q, in_2);
endmodule

module nand_not (
  input  in_1,
  output out_2
);

  nand nand_1 (out_2, in_1, in_1);
endmodule

module nand_and (
  input  in_1,
  input  in_2,
  output out_3
);

  wire nand_1_out;

  nand nand_1 (nand_1_out, in_1, in_2);
  nand_not nand_not_1 (.in_1(nand_1_out), .out_2(out_3));
endmodule

module nand_or (
  input  in_1,
  input  in_2,
  output out_3
);

  wire nand_not_1_out_2, nand_not_2_out_2;

  nand_not nand_not_1 (.in_1(in_1), .out_2(nand_not_1_out_2));
  nand_not nand_not_2 (.in_1(in_2), .out_2(nand_not_2_out_2));
  nand nand_1 (out_3, nand_not_1_out_2, nand_not_2_out_2);
endmodule
