// Logisim project nand_xor.circ as structural Verilog: 1 circuit, main circuit main
module main (
);

  wire button_1_out, nand_1_out, nand_2_out, nand_3_out, nand_4_out;

  Button button_1 (.out(button_1_out));
  nand nand_1 (nand_1_out, 1'b1, button_1_out);
  nand nand_2 (nand_2_out, 1'b1, nand_1_out);
  nand nand_3 (nand_3_out, nand_1_out, button_1_out);
  nand nand_4 (nand_4_out, nand_2_out, nand_3_out);
  LED led_1 (.in(nand_4_out));
endmodule
